// Logisim project CPU.circ as structural Verilog: 2 circuits, main circuit main
module main (
  output RESTO,
  output out_2,
  output out_3,
  output out_4,
  output REG__A,
  output out_6,
  output out_7,
  output out_8,
  output out_9,
  output out_10,
  output out_11,
  output out_12,
  output REG__B,
  output out_14,
  output out_15,
  output out_16,
  output out_17,
  output out_18,
  output out_19,
  output IR,
  output out_21,
  output out_22,
  output out_23,
  output out_24,
  output out_25
);

  wire alu_1_num_0, alu_1_num_neg, alu_1_resto, alu_1_resto_div, and_1_out, and_2_out, and_3_out, and_4_out,
       and_5_out, and_6_out, and_7_out, and_8_out, and_9_out, and_10_out, and_11_out, and_12_out, and_13_out,
       and_14_out, and_15_out, and_16_out, and_17_out, and_18_out, and_19_out, and_20_out, and_21_out,
       and_22_out, and_23_out, and_24_out, and_25_out, and_26_out, and_27_out, and_28_out, and_29_out,
       and_30_out, and_31_out, and_33_out, and_34_out, and_35_out, and_36_out, and_39_out, and_40_out,
       and_41_out, and_42_out, and_44_out, and_46_out, and_48_out, and_49_out, and_50_out, and_52_out,
       and_54_out, and_56_out, and_58_out, and_60_out, and_61_out, and_62_out, and_66_out, and_67_out,
       and_68_out, and_69_out, and_70_out, and_71_out, and_72_out, and_73_out, and_74_out, and_75_out,
       and_76_out, and_77_out, and_78_out, and_79_out, and_80_out, and_81_out, and_82_out, buffer_1_out,
       button_1_out, clock_1_out, controlled_buffer_19_out, d_ff_1_q, d_ff_2_q, d_ff_3_q, or_5_out,
       xnor_1_out, xnor_2_out, xnor_3_out, xor_1_out, xor_2_out, xor_3_out, xor_4_out, xor_5_out, xor_6_out,
       xor_7_out;
  wire [1:0] and_32_out, controlled_buffer_1_out_2, controlled_buffer_1_out_3;
  wire [3:1] d_ff_5_q;
  wire [5:4] and_63_out, and_64_out, and_65_out, not_27_out, or_6_out, or_7_out, or_8_out, undriven;
  wire [5:5] not_26_out;
  wire [6:0] alu_1_out_4_2;
  wire [6:6] not_1_out;
  wire [7:0] controlled_buffer_61_out, counter_1_q, multiplexer_1_out, multiplexer_2_out, multiplexer_3_out;
  wire [7:6] and_43_out;
  wire [7:7] alu_1_out_4;
  wire [13:6] and_45_out, and_47_out, and_51_out, and_53_out, and_55_out, and_57_out;
  wire [16:14] and_59_out;
  wire [16:15] not_4_out;
  wire [16:16] not_5_out, not_24_out;
  wire [18:17] or_3_out;
  wire [19:17] and_37_out;
  wire [20:0] controlled_buffer_1_out;

  Clock clock_1 (.out(clock_1_out));
  Button button_1 (.out(button_1_out));
  D_Flip_Flop d_ff_1 (.clk(button_1_out), .D(clock_1_out), .Q(d_ff_1_q));  // open: Qn, preset, en, reset
  xnor xnor_1 (xnor_1_out, d_ff_1_q, clock_1_out);
  Register register_1 (
    .D({alu_1_out_4[7], alu_1_out_4_2}), .en(controlled_buffer_1_out[7]),
    .Q({out_2, out_3, out_4, REG__A, out_6, out_7, out_8, out_9}), .clk(xnor_1_out), .clr(button_1_out));
  Register register_2 (
    .D({alu_1_out_4[7], alu_1_out_4_2}), .en(controlled_buffer_1_out[6]),
    .Q({out_10, out_11, out_12, REG__B, out_14, out_15, out_16, out_17}), .clk(xnor_1_out), .clr(button_1_out));
  assign {controlled_buffer_1_out[20:17], controlled_buffer_1_out_3, controlled_buffer_1_out_2, controlled_buffer_1_out[12:0]} = and_2_out ? {{15{1'b0}}, undriven, 4'b1001} : 21'bz;  // Controlled_Buffer controlled_buffer_1
  D_Flip_Flop d_ff_2 (
    .clk(xnor_1_out), .D(controlled_buffer_19_out), .Q(d_ff_2_q), .preset(button_1_out));  // open: Qn, en, reset
  and and_1 (and_1_out, ~and_2_out, ~d_ff_3_q);  // AND_Gate
  Multiplexer #(.select(2), .width(8), .enable("false")) multiplexer_1 (
    .in0({out_2, out_3, out_4, REG__A, out_6, out_7, out_8, out_9}),
    .in1({out_10, out_11, out_12, REG__B, out_14, out_15, out_16, out_17}), .in2(controlled_buffer_61_out),
    .in3({8{1'b0}}), .out(multiplexer_1_out), .sel(controlled_buffer_1_out_3));
  Multiplexer #(.select(2), .width(8), .enable("false")) multiplexer_2 (
    .in0({out_10, out_11, out_12, REG__B, out_14, out_15, out_16, out_17}),
    .in1({out_2, out_3, out_4, REG__A, out_6, out_7, out_8, out_9}), .in2({8{1'b0}}),
    .out(multiplexer_2_out), .sel(controlled_buffer_1_out_2));  // open: in3
  buf buffer_1 (buffer_1_out, xnor_1_out);
  and and_2 (and_2_out, d_ff_2_q, xnor_1_out);
  and and_3 (and_3_out, d_ff_2_q, ~controlled_buffer_19_out);  // AND_Gate
  and and_4 (and_4_out, and_66_out, and_1_out);
  and and_5 (and_5_out, and_4_out, xor_1_out);
  and and_6 (and_6_out, and_67_out, and_1_out);
  and and_7 (and_7_out, and_68_out, and_1_out);
  and and_8 (and_8_out, and_69_out, and_1_out);
  and and_9 (and_9_out, and_8_out, xor_2_out);
  and and_10 (and_10_out, and_70_out, and_1_out);
  and and_11 (and_11_out, and_10_out, xor_3_out);
  and and_12 (and_12_out, and_71_out, and_1_out);
  and and_13 (and_13_out, and_12_out, out_25, ~out_24);  // AND_Gate
  and and_14 (and_14_out, and_72_out, and_1_out);
  and and_15 (and_15_out, and_14_out, out_25, ~out_24);  // AND_Gate
  and and_16 (and_16_out, and_73_out, and_1_out);
  and and_17 (and_17_out, and_16_out, not_4_out[16]);
  and and_18 (and_18_out, and_74_out, and_1_out);
  and and_19 (and_19_out, and_18_out, xor_4_out);
  and and_20 (and_20_out, and_75_out, and_1_out);
  and and_21 (and_21_out, and_20_out, xor_5_out);
  and and_22 (and_22_out, and_76_out, and_1_out);
  and and_23 (and_23_out, and_22_out, xor_6_out);
  and and_24 (and_24_out, and_77_out, and_1_out);
  and and_25 (and_25_out, and_24_out, xor_7_out);
  and and_26 (and_26_out, and_78_out, and_1_out);
  and and_27 (and_27_out, and_79_out, and_1_out);
  and and_28 (and_28_out, and_80_out, and_1_out);
  and and_29 (and_29_out, and_81_out, and_1_out);
  and and_30 (and_30_out, and_29_out, xnor_3_out);
  and and_31 (and_31_out, and_82_out, and_1_out);
  and and_32 (and_32_out[0], and_31_out, and_82_out);
  xnor xnor_2 (xnor_2_out, xnor_1_out, buffer_1_out);
  D_Flip_Flop d_ff_3 (.clk(xnor_1_out), .D(and_3_out), .Q(d_ff_3_q), .reset(button_1_out));  // open: Qn, preset, en
  assign {controlled_buffer_1_out[20:17], controlled_buffer_1_out_3, controlled_buffer_1_out_2, controlled_buffer_1_out[12:0]} = and_5_out ? {4'b0000, {2{out_24}}, out_25, {6{1'b0}}, out_24, out_25, 6'b001001} : 21'bz;  // Controlled_Buffer controlled_buffer_2
  not not_1 (not_1_out[6], out_25);
  assign {controlled_buffer_1_out[20:17], controlled_buffer_1_out_3, controlled_buffer_1_out_2, controlled_buffer_1_out[12:0]} = and_6_out ? {13'h140, out_25, not_1_out[6], 3'b000, out_25, 2'b01} : 21'bz;  // Controlled_Buffer controlled_buffer_3
  assign {controlled_buffer_1_out[20:17], controlled_buffer_1_out_3, controlled_buffer_1_out_2, controlled_buffer_1_out[12:0]} = and_7_out ? {4'b0000, {2{not_5_out[16]}}, out_25, 11'h200, out_25, 2'b00} : 21'bz;  // Controlled_Buffer controlled_buffer_4
  assign {controlled_buffer_1_out[20:17], controlled_buffer_1_out_3, controlled_buffer_1_out_2, controlled_buffer_1_out[12:0]} = and_9_out ? {2'b00, out_24, out_25, 9'h6, out_25, out_24, 6'b001001} : 21'bz;  // Controlled_Buffer controlled_buffer_5
  assign {controlled_buffer_1_out[20:17], controlled_buffer_1_out_3, controlled_buffer_1_out_2, controlled_buffer_1_out[12:0]} = and_11_out ? {13'ha, out_25, out_24, 6'b001001} : 21'bz;  // Controlled_Buffer controlled_buffer_6
  not not_2 (and_63_out[5], and_63_out[4]);
  assign {controlled_buffer_1_out[20:17], controlled_buffer_1_out_3, controlled_buffer_1_out_2, controlled_buffer_1_out[12:0]} = and_13_out ? {15'h500, and_63_out, 4'b1001} : 21'bz;  // Controlled_Buffer controlled_buffer_7
  not not_3 (or_6_out[5], or_6_out[4]);
  assign {controlled_buffer_1_out[20:17], controlled_buffer_1_out_3, controlled_buffer_1_out_2, controlled_buffer_1_out[12:0]} = and_15_out ? {15'h500, or_6_out, 4'b1001} : 21'bz;  // Controlled_Buffer controlled_buffer_8
  assign {controlled_buffer_1_out[20:17], controlled_buffer_1_out_3, controlled_buffer_1_out_2, controlled_buffer_1_out[12:0]} = and_17_out ? {4'b0000, not_4_out, not_4_out[16], 14'h19} : 21'bz;  // Controlled_Buffer controlled_buffer_9
  assign {controlled_buffer_1_out[20:17], controlled_buffer_1_out_3, controlled_buffer_1_out_2, controlled_buffer_1_out[12:0]} = and_19_out ? {3'b010, out_24, 9'h3, out_25, out_24, 6'b001001} : 21'bz;  // Controlled_Buffer controlled_buffer_10
  assign {controlled_buffer_1_out[20:17], controlled_buffer_1_out_3, controlled_buffer_1_out_2, controlled_buffer_1_out[12:0]} = and_21_out ? {13'h602, out_25, out_24, 6'b001001} : 21'bz;  // Controlled_Buffer controlled_buffer_11
  assign {controlled_buffer_1_out[20:17], controlled_buffer_1_out_3, controlled_buffer_1_out_2, controlled_buffer_1_out[12:0]} = and_23_out ? {3'b011, out_24, 9'h2, out_25, out_24, 6'b001001} : 21'bz;  // Controlled_Buffer controlled_buffer_12
  assign {controlled_buffer_1_out[20:17], controlled_buffer_1_out_3, controlled_buffer_1_out_2, controlled_buffer_1_out[12:0]} = and_25_out ? {3'b100, out_24, 9'h2, out_25, out_24, 6'b001001} : 21'bz;  // Controlled_Buffer controlled_buffer_13
  assign {controlled_buffer_1_out[20:17], controlled_buffer_1_out_3, controlled_buffer_1_out_2, controlled_buffer_1_out[12:0]} = and_26_out ? {1'b1, and_37_out, 17'h689} : 21'bz;  // Controlled_Buffer controlled_buffer_14
  assign {controlled_buffer_1_out[20:17], controlled_buffer_1_out_3, controlled_buffer_1_out_2, controlled_buffer_1_out[12:0]} = and_27_out ? {2'b11, or_3_out, 17'h689} : 21'bz;  // Controlled_Buffer controlled_buffer_15
  assign {controlled_buffer_1_out[20:17], controlled_buffer_1_out_3, controlled_buffer_1_out_2, controlled_buffer_1_out[12:0]} = and_28_out ? 21'h1c0db : 21'bz;  // Controlled_Buffer controlled_buffer_16
  assign {controlled_buffer_1_out[20:17], controlled_buffer_1_out_3, controlled_buffer_1_out_2, controlled_buffer_1_out[12:0]} = and_30_out ? 21'h14029 : 21'bz;  // Controlled_Buffer controlled_buffer_17
  assign {controlled_buffer_1_out[20:17], controlled_buffer_1_out_3, controlled_buffer_1_out_2, controlled_buffer_1_out[12:0]} = and_32_out[0] ? 21'h14009 : 21'bz;  // Controlled_Buffer controlled_buffer_18
  Counter counter_1 (
    .load(controlled_buffer_1_out[4]), .D({alu_1_out_4[7], alu_1_out_4_2}),
    .count(controlled_buffer_1_out[5]), .Q(counter_1_q), .clk(xnor_2_out), .clr(button_1_out));  // open: carry
  assign controlled_buffer_19_out = and_5_out ? 1'b1 : 1'bz;  // Controlled_Buffer controlled_buffer_19
  assign controlled_buffer_19_out = and_6_out ? 1'b1 : 1'bz;  // Controlled_Buffer controlled_buffer_20
  assign controlled_buffer_19_out = and_7_out ? 1'b1 : 1'bz;  // Controlled_Buffer controlled_buffer_21
  assign controlled_buffer_19_out = and_9_out ? 1'b1 : 1'bz;  // Controlled_Buffer controlled_buffer_22
  assign controlled_buffer_19_out = and_11_out ? 1'b1 : 1'bz;  // Controlled_Buffer controlled_buffer_23
  assign controlled_buffer_19_out = and_13_out ? 1'b1 : 1'bz;  // Controlled_Buffer controlled_buffer_24
  assign controlled_buffer_19_out = and_15_out ? 1'b1 : 1'bz;  // Controlled_Buffer controlled_buffer_25
  nor nor_1 (not_4_out[16], out_25, out_24);
  not not_4 (not_4_out[15], not_4_out[16]);
  assign controlled_buffer_19_out = and_17_out ? 1'b1 : 1'bz;  // Controlled_Buffer controlled_buffer_26
  assign controlled_buffer_19_out = and_19_out ? 1'b1 : 1'bz;  // Controlled_Buffer controlled_buffer_27
  assign controlled_buffer_19_out = and_21_out ? 1'b1 : 1'bz;  // Controlled_Buffer controlled_buffer_28
  assign controlled_buffer_19_out = and_23_out ? 1'b1 : 1'bz;  // Controlled_Buffer controlled_buffer_29
  assign controlled_buffer_19_out = and_25_out ? 1'b1 : 1'bz;  // Controlled_Buffer controlled_buffer_30
  assign controlled_buffer_19_out = and_26_out ? 1'b1 : 1'bz;  // Controlled_Buffer controlled_buffer_31
  assign controlled_buffer_19_out = and_27_out ? 1'b1 : 1'bz;  // Controlled_Buffer controlled_buffer_32
  assign controlled_buffer_19_out = and_28_out ? 1'b1 : 1'bz;  // Controlled_Buffer controlled_buffer_33
  assign controlled_buffer_19_out = and_30_out ? 1'b1 : 1'bz;  // Controlled_Buffer controlled_buffer_34
  assign controlled_buffer_19_out = and_32_out[0] ? 1'b1 : 1'bz;  // Controlled_Buffer controlled_buffer_35
  xor xor_1 (xor_1_out, out_25, out_24);
  not not_5 (not_5_out[16], out_25);
  xor xor_2 (xor_2_out, out_25, out_24);
  xor xor_3 (xor_3_out, out_25, out_24);
  not not_6 (and_64_out[5], and_64_out[4]);
  and and_33 (and_33_out, and_12_out, ~out_25, out_24);  // AND_Gate
  assign {controlled_buffer_1_out[20:17], controlled_buffer_1_out_3, controlled_buffer_1_out_2, controlled_buffer_1_out[12:0]} = and_33_out ? {15'h500, and_64_out, 4'b1001} : 21'bz;  // Controlled_Buffer controlled_buffer_36
  not not_7 (or_7_out[5], or_7_out[4]);
  and and_34 (and_34_out, and_14_out, ~out_25, out_24);  // AND_Gate
  assign {controlled_buffer_1_out[20:17], controlled_buffer_1_out_3, controlled_buffer_1_out_2, controlled_buffer_1_out[12:0]} = and_34_out ? {15'h500, or_7_out, 4'b1001} : 21'bz;  // Controlled_Buffer controlled_buffer_37
  and and_35 (and_35_out, ~not_4_out[16], and_16_out);  // AND_Gate
  assign {controlled_buffer_1_out[20:17], controlled_buffer_1_out_3, controlled_buffer_1_out_2, controlled_buffer_1_out[12:0]} = and_35_out ? {4'b0000, {2{and_59_out[16]}}, and_59_out[14], 14'h19} : 21'bz;  // Controlled_Buffer controlled_buffer_38
  xor xor_4 (xor_4_out, out_25, out_24);
  xor xor_5 (xor_5_out, out_25, out_24);
  xor xor_6 (xor_6_out, out_25, out_24);
  xor xor_7 (xor_7_out, out_25, out_24);
  or or_1 (and_37_out[18], and_37_out[17], and_39_out);
  or or_2 (or_3_out[18], and_40_out, and_41_out);
  or or_3 (or_3_out[17], and_41_out, and_42_out);
  and and_36 (and_36_out, ~out_25, and_30_out, ~out_24);  // AND_Gate
  or or_4 (and_32_out[1], and_36_out, and_60_out);
  ALU alu_1 (
    .S(controlled_buffer_1_out[20:17]), .A(multiplexer_1_out), .B(multiplexer_2_out),
    .out_4({alu_1_out_4[7], alu_1_out_4_2}), .RESTO(alu_1_resto), .RESTO_DIV(alu_1_resto_div),
    .NUM_NEG(alu_1_num_neg), .NUM_0(alu_1_num_0));
  assign controlled_buffer_19_out = and_33_out ? 1'b1 : 1'bz;  // Controlled_Buffer controlled_buffer_39
  assign controlled_buffer_19_out = and_34_out ? 1'b1 : 1'bz;  // Controlled_Buffer controlled_buffer_40
  assign controlled_buffer_19_out = and_35_out ? 1'b1 : 1'bz;  // Controlled_Buffer controlled_buffer_41
  and and_37 (and_37_out[17], out_25, ~out_24);  // AND_Gate
  and and_38 (and_37_out[19], ~out_25, out_24);  // AND_Gate
  and and_39 (and_39_out, ~out_25, ~out_24);  // AND_Gate
  and and_40 (and_40_out, out_25, ~out_24);  // AND_Gate
  and and_41 (and_41_out, ~out_25, out_24);  // AND_Gate
  and and_42 (and_42_out, ~out_25, ~out_24);  // AND_Gate
  Multiplexer #(.select(2), .width(8), .enable("false")) multiplexer_3 (
    .in0({out_2, out_3, out_4, REG__A, out_6, out_7, out_8, out_9}),
    .in1({out_10, out_11, out_12, REG__B, out_14, out_15, out_16, out_17}), .in2(counter_1_q),
    .out(multiplexer_3_out), .sel(controlled_buffer_1_out[3:2]));  // open: in3
  and and_43 (and_43_out[6], out_25, out_24);
  not not_8 (and_43_out[7], and_43_out[6]);
  and and_44 (and_44_out, and_4_out, ~xor_1_out);  // AND_Gate
  assign {controlled_buffer_1_out[20:17], controlled_buffer_1_out_3, controlled_buffer_1_out_2, controlled_buffer_1_out[12:0]} = and_44_out ? {13'h140, and_43_out, 6'b101001} : 21'bz;  // Controlled_Buffer controlled_buffer_42
  and and_45 (and_45_out[6], out_25, out_24);
  not not_9 (and_45_out[7], and_45_out[6]);
  and and_46 (and_46_out, and_8_out, ~xor_2_out);  // AND_Gate
  assign {controlled_buffer_1_out[20:17], controlled_buffer_1_out_3, controlled_buffer_1_out_2, controlled_buffer_1_out[12:0]} = and_46_out ? {7'b0010100, and_45_out[13], 5'b00110, and_45_out[7:6], 6'b101001} : 21'bz;  // Controlled_Buffer controlled_buffer_43
  and and_47 (and_47_out[6], out_25, out_24);
  not not_10 (and_47_out[7], and_47_out[6]);
  and and_48 (and_48_out, and_10_out, ~xor_3_out);  // AND_Gate
  assign {controlled_buffer_1_out[20:17], controlled_buffer_1_out_3, controlled_buffer_1_out_2, controlled_buffer_1_out[12:0]} = and_48_out ? {7'b0000100, and_47_out[13], 5'b01010, and_47_out[7:6], 6'b101001} : 21'bz;  // Controlled_Buffer controlled_buffer_44
  not not_11 (and_65_out[5], and_65_out[4]);
  and and_49 (and_49_out, and_12_out, ~out_25, ~out_24);  // AND_Gate
  assign {controlled_buffer_1_out[20:17], controlled_buffer_1_out_3, controlled_buffer_1_out_2, controlled_buffer_1_out[12:0]} = and_49_out ? {15'h500, and_65_out, 4'b1001} : 21'bz;  // Controlled_Buffer controlled_buffer_45
  not not_12 (or_8_out[5], or_8_out[4]);
  and and_50 (and_50_out, and_14_out, ~out_25, ~out_24);  // AND_Gate
  assign {controlled_buffer_1_out[20:17], controlled_buffer_1_out_3, controlled_buffer_1_out_2, controlled_buffer_1_out[12:0]} = and_50_out ? {15'h500, or_8_out, 4'b1001} : 21'bz;  // Controlled_Buffer controlled_buffer_46
  not not_13 (and_59_out[16], and_59_out[14]);
  and and_51 (and_51_out[6], out_25, out_24);
  not not_14 (and_51_out[7], and_51_out[6]);
  and and_52 (and_52_out, and_18_out, ~xor_4_out);  // AND_Gate
  assign {controlled_buffer_1_out[20:17], controlled_buffer_1_out_3, controlled_buffer_1_out_2, controlled_buffer_1_out[12:0]} = and_52_out ? {7'b0101100, and_51_out[13], 5'b00011, and_51_out[7:6], 6'b101001} : 21'bz;  // Controlled_Buffer controlled_buffer_47
  and and_53 (and_53_out[6], out_25, out_24);
  not not_15 (and_53_out[7], and_53_out[6]);
  and and_54 (and_54_out, and_20_out, ~xor_5_out);  // AND_Gate
  assign {controlled_buffer_1_out[20:17], controlled_buffer_1_out_3, controlled_buffer_1_out_2, controlled_buffer_1_out[12:0]} = and_54_out ? {7'b0011100, and_53_out[13], 5'b00010, and_53_out[7:6], 6'b101001} : 21'bz;  // Controlled_Buffer controlled_buffer_48
  and and_55 (and_55_out[6], out_25, out_24);
  not not_16 (and_55_out[7], and_55_out[6]);
  and and_56 (and_56_out, and_22_out, ~xor_6_out);  // AND_Gate
  assign {controlled_buffer_1_out[20:17], controlled_buffer_1_out_3, controlled_buffer_1_out_2, controlled_buffer_1_out[12:0]} = and_56_out ? {7'b0110100, and_55_out[13], 5'b00010, and_55_out[7:6], 6'b101001} : 21'bz;  // Controlled_Buffer controlled_buffer_49
  and and_57 (and_57_out[6], out_25, out_24);
  not not_17 (and_57_out[7], and_57_out[6]);
  and and_58 (and_58_out, and_24_out, ~xor_7_out);  // AND_Gate
  assign {controlled_buffer_1_out[20:17], controlled_buffer_1_out_3, controlled_buffer_1_out_2, controlled_buffer_1_out[12:0]} = and_58_out ? {7'b1000100, and_57_out[13], 5'b00010, and_57_out[7:6], 6'b101001} : 21'bz;  // Controlled_Buffer controlled_buffer_50
  xnor xnor_3 (xnor_3_out, out_25, out_24);
  assign controlled_buffer_19_out = and_44_out ? 1'b1 : 1'bz;  // Controlled_Buffer controlled_buffer_51
  not not_18 (and_45_out[13], and_45_out[6]);
  assign controlled_buffer_19_out = and_46_out ? 1'b1 : 1'bz;  // Controlled_Buffer controlled_buffer_52
  not not_19 (and_47_out[13], and_47_out[6]);
  assign controlled_buffer_19_out = and_48_out ? 1'b1 : 1'bz;  // Controlled_Buffer controlled_buffer_53
  assign controlled_buffer_19_out = and_49_out ? 1'b1 : 1'bz;  // Controlled_Buffer controlled_buffer_54
  assign controlled_buffer_19_out = and_50_out ? 1'b1 : 1'bz;  // Controlled_Buffer controlled_buffer_55
  and and_59 (and_59_out[14], ~out_25, out_24);  // AND_Gate
  not not_20 (and_51_out[13], and_51_out[6]);
  assign controlled_buffer_19_out = and_52_out ? 1'b1 : 1'bz;  // Controlled_Buffer controlled_buffer_56
  not not_21 (and_53_out[13], and_53_out[6]);
  assign controlled_buffer_19_out = and_54_out ? 1'b1 : 1'bz;  // Controlled_Buffer controlled_buffer_57
  not not_22 (and_55_out[13], and_55_out[6]);
  assign controlled_buffer_19_out = and_56_out ? 1'b1 : 1'bz;  // Controlled_Buffer controlled_buffer_58
  not not_23 (and_57_out[13], and_57_out[6]);
  assign controlled_buffer_19_out = and_58_out ? 1'b1 : 1'bz;  // Controlled_Buffer controlled_buffer_59
  and and_60 (and_60_out, and_29_out, ~xnor_3_out);  // AND_Gate
  assign {controlled_buffer_1_out[20:17], controlled_buffer_1_out_3, controlled_buffer_1_out_2, controlled_buffer_1_out[12:0]} = and_60_out ? {4'b0000, {2{not_24_out[16]}}, out_25, 14'h9} : 21'bz;  // Controlled_Buffer controlled_buffer_60
  assign controlled_buffer_61_out = controlled_buffer_1_out[12] ? {alu_1_out_4[7], alu_1_out_4_2} : 8'bz;  // Controlled_Buffer controlled_buffer_61
  RAM ram_1 (
    .addr(multiplexer_3_out), .data(controlled_buffer_61_out), .sel(1'b1), .clk(xnor_1_out),
    .ld(controlled_buffer_1_out[0]), .clr(controlled_buffer_1_out[1]));
  and and_61 (and_61_out, and_12_out, out_25, out_24);
  assign {controlled_buffer_1_out[20:17], controlled_buffer_1_out_3, controlled_buffer_1_out_2, controlled_buffer_1_out[12:0]} = and_61_out ? {15'h500, not_27_out, 4'b1001} : 21'bz;  // Controlled_Buffer controlled_buffer_62
  and and_62 (and_62_out, and_14_out, out_25, out_24);
  assign {controlled_buffer_1_out[20:17], controlled_buffer_1_out_3, controlled_buffer_1_out_2, controlled_buffer_1_out[12:0]} = and_62_out ? {15'h500, not_26_out[5], d_ff_5_q[3], 4'b1001} : 21'bz;  // Controlled_Buffer controlled_buffer_63
  not not_24 (not_24_out[16], out_25);
  assign controlled_buffer_19_out = and_60_out ? 1'b1 : 1'bz;  // Controlled_Buffer controlled_buffer_64
  D_Flip_Flop d_ff_4 (
    .clk(xnor_1_out), .D(alu_1_resto), .Q(RESTO), .en(controlled_buffer_1_out[11]), .reset(button_1_out));  // open: Qn, preset
  TTY #(.rows(15)) tty_1 (.data(alu_1_out_4_2), .clk(xnor_1_out), .we(and_32_out[1]), .clr(or_5_out));
  not not_25 (not_27_out[5], not_27_out[4]);
  assign controlled_buffer_19_out = and_61_out ? 1'b1 : 1'bz;  // Controlled_Buffer controlled_buffer_65
  not not_26 (not_26_out[5], d_ff_5_q[3]);
  assign controlled_buffer_19_out = and_62_out ? 1'b1 : 1'bz;  // Controlled_Buffer controlled_buffer_66
  D_Flip_Flop d_ff_5 (
    .clk(xnor_1_out), .D(alu_1_num_neg), .Q(d_ff_5_q[1]), .en(controlled_buffer_1_out[10]),
    .reset(button_1_out));  // open: Qn, preset
  or or_5 (or_5_out, and_32_out[0], button_1_out);
  D_Flip_Flop d_ff_6 (
    .clk(xnor_1_out), .D(alu_1_num_0), .Q(d_ff_5_q[2]), .en(controlled_buffer_1_out[9]), .reset(button_1_out));  // open: Qn, preset
  and and_63 (and_63_out[4], ~d_ff_5_q[1], ~d_ff_5_q[2]);  // AND_Gate
  and and_64 (and_64_out[4], d_ff_5_q[1], ~d_ff_5_q[2]);  // AND_Gate
  and and_65 (and_65_out[4], ~d_ff_5_q[1], d_ff_5_q[2]);  // AND_Gate
  not not_27 (not_27_out[4], d_ff_5_q[3]);
  or or_6 (or_6_out[4], d_ff_5_q[1], d_ff_5_q[2]);
  or or_7 (or_7_out[4], ~d_ff_5_q[1], d_ff_5_q[2]);  // OR_Gate
  or or_8 (or_8_out[4], d_ff_5_q[1], ~d_ff_5_q[2]);  // OR_Gate
  D_Flip_Flop d_ff_7 (
    .clk(xnor_1_out), .D(alu_1_resto_div), .Q(d_ff_5_q[3]), .en(controlled_buffer_1_out[8]),
    .reset(button_1_out));  // open: Qn, preset
  Register #(.trigger("falling")) register_3 (
    .D(controlled_buffer_61_out), .en(d_ff_2_q),
    .Q({out_18, out_19, IR, out_21, out_22, out_23, out_24, out_25}), .clk(xnor_1_out), .clr(button_1_out));
  and and_66 (and_66_out, ~out_23, ~out_22, ~out_21, ~IR, ~out_19, ~out_18);  // AND_Gate
  and and_67 (and_67_out, out_23, ~out_22, ~out_21, ~IR, ~out_19, ~out_18);  // AND_Gate
  and and_68 (and_68_out, ~out_23, out_22, ~out_21, ~IR, ~out_19, ~out_18);  // AND_Gate
  and and_69 (and_69_out, ~out_23, ~out_22, out_21, ~IR, ~out_19, ~out_18);  // AND_Gate
  and and_70 (and_70_out, ~out_23, out_22, out_21, ~IR, ~out_19, ~out_18);  // AND_Gate
  and and_71 (and_71_out, ~out_23, ~out_22, ~out_21, IR, ~out_19, ~out_18);  // AND_Gate
  and and_72 (and_72_out, out_23, ~out_22, ~out_21, IR, ~out_19, ~out_18);  // AND_Gate
  and and_73 (and_73_out, ~out_23, out_22, ~out_21, IR, ~out_19, ~out_18);  // AND_Gate
  and and_74 (and_74_out, ~out_23, ~out_22, out_21, IR, ~out_19, ~out_18);  // AND_Gate
  and and_75 (and_75_out, ~out_23, out_22, out_21, IR, ~out_19, ~out_18);  // AND_Gate
  and and_76 (and_76_out, ~out_23, ~out_22, ~out_21, ~IR, out_19, ~out_18);  // AND_Gate
  and and_77 (and_77_out, ~out_23, ~out_22, out_21, ~IR, out_19, ~out_18);  // AND_Gate
  and and_78 (and_78_out, ~out_23, ~out_22, ~out_21, IR, out_19, ~out_18);  // AND_Gate
  and and_79 (and_79_out, ~out_23, ~out_22, out_21, IR, out_19, ~out_18);  // AND_Gate
  and and_80 (and_80_out, out_23, out_22, out_21, IR, out_19, out_18);
  and and_81 (and_81_out, ~out_23, ~out_22, ~out_21, ~IR, ~out_19, out_18);  // AND_Gate
  and and_82 (and_82_out, ~out_23, ~out_22, out_21, ~IR, ~out_19, out_18);  // AND_Gate

  // Notes on the sheet:
  //   CK
  //   CLEAR
  //   A
  //   B
  //   MOVE TO
  //   UNC. JMP
  //   MOVE (r)->r 
  //   MOVE r->(r) 
  //   SUB r & r
  //   ADD r & r
  //   DIV r & r
  //   MOL r & r
  //   C. A2 r
  //   NOT r
  //   AND/ OR/ XOR
  //   NAND/ NOR/ XNOR
  //   RESET
  //   SCREEN WRITE imm.
  //   SCREEN CLEAR/ WRITE imm.
  //   F-BUS
  //   IND. JMP
  //   A-BUS
  //   IMM. MOVE
  //   SUB imm
  //   ADD imm
  //   DIV imm
  //   MOL imm
  //   C. A2 imm
  //   NOT imm
  //   SCREEN WRITE r
  //   SCREEN WRITE r
  //   D-BUS
  //   a>b
  //   a<b
  //   a=b
  //   a%b0
  //   a<=b
  //   a>=b
  //   a!=b
  //   a%b!0
  //   FLAGS
  //   IR
  //   MOVE DEFAULT
  //   MOVE CUSTOM REG
  //   MOVE CUSTOM RAM
  //   SUB
  //   ADD
  //   JMP IF
  //   JMP IF NOT
  //   UNC./ IND. JMP
  //   DIV.
  //   MOL.
  //   C. A2
  //   NOT
  //   AND/ OR/ XOR
  //   NAND/ NOR/ XOR
  //   RESET
  //   SCREEN WRITE
  //   SCREEN CLEAR
endmodule

module ALU (
  input  [7:0] A,
  input  [7:0] B,
  input  [3:0] S,
  output [7:0] out_4,
  output RESTO,
  output NUM_NEG,
  output NUM_0,
  output RESTO_DIV
);

  wire adder_1_cout, and_2_out, and_3_out, bitfinder_1_found, bitfinder_2_found, decoder_1_out0,
       decoder_1_out1, decoder_1_out2, decoder_1_out3, decoder_1_out4, decoder_1_out5, decoder_1_out6,
       decoder_1_out7, decoder_1_out8, decoder_1_out9, decoder_1_out10, decoder_1_out11, decoder_1_out12,
       decoder_1_out13, decoder_1_out14, decoder_1_out15, subtractor_1_bout, subtractor_2_bout;
  wire [7:0] adder_1_out, and_1_out, divider_1_out, divider_1_rem, divider_2_out, divider_2_rem,
       multiplier_1_out, nand_1_out, negator_1_out, negator_2_out, nor_1_out, not_1_out, not_2_out, or_2_out,
       subtractor_1_out, subtractor_2_out, xnor_1_out, xor_1_out;

  Decoder #(.select(4), .enable("false")) decoder_1 (
    .out0(decoder_1_out0), .out1(decoder_1_out1), .out2(decoder_1_out2), .out3(decoder_1_out3),
    .out4(decoder_1_out4), .out5(decoder_1_out5), .out6(decoder_1_out6), .out7(decoder_1_out7),
    .out8(decoder_1_out8), .out9(decoder_1_out9), .out10(decoder_1_out10), .out11(decoder_1_out11),
    .out12(decoder_1_out12), .out13(decoder_1_out13), .out14(decoder_1_out14), .out15(decoder_1_out15),
    .sel(S));
  // OR_Gate or_1 is placed but not wired
  Adder adder_1 (.a(A), .b(B), .out(adder_1_out), .cout(adder_1_cout));  // open: cin
  Subtractor subtractor_1 (.a(A), .b(B), .out(subtractor_1_out), .bout(subtractor_1_bout));  // open: bin
  Subtractor subtractor_2 (.a(B), .b(A), .out(subtractor_2_out), .bout(subtractor_2_bout));  // open: bin
  Multiplier multiplier_1 (.a(A), .b(B), .out(multiplier_1_out));  // open: cin, cout
  Divider divider_1 (.a(A), .b(B), .out(divider_1_out), .rem(divider_1_rem));  // open: upper
  Divider divider_2 (.a(B), .b(A), .out(divider_2_out), .rem(divider_2_rem));  // open: upper
  Negator negator_1 (.in(A), .out(negator_1_out));
  Negator negator_2 (.in(B), .out(negator_2_out));
  assign not_1_out = ~A;  // NOT_Gate not_1, 8 bits wide
  assign not_2_out = ~B;  // NOT_Gate not_2, 8 bits wide
  assign and_1_out = A & B;  // AND_Gate and_1, 8 bits wide
  assign or_2_out = A | B;  // OR_Gate or_2, 8 bits wide
  assign xor_1_out = A ^ B;  // XOR_Gate xor_1, 8 bits wide
  assign nand_1_out = ~(A & B);  // NAND_Gate nand_1, 8 bits wide
  assign nor_1_out = ~(A | B);  // NOR_Gate nor_1, 8 bits wide
  assign xnor_1_out = ~(A ^ B);  // XNOR_Gate xnor_1, 8 bits wide
  assign out_4 = decoder_1_out0 ? adder_1_out : 8'bz;  // Controlled_Buffer controlled_buffer_1
  assign RESTO = decoder_1_out0 ? adder_1_cout : 1'bz;  // Controlled_Buffer controlled_buffer_2
  assign out_4 = decoder_1_out1 ? subtractor_1_out : 8'bz;  // Controlled_Buffer controlled_buffer_3
  assign NUM_NEG = decoder_1_out1 ? subtractor_1_bout : 1'bz;  // Controlled_Buffer controlled_buffer_4
  assign out_4 = decoder_1_out2 ? subtractor_2_out : 8'bz;  // Controlled_Buffer controlled_buffer_5
  assign NUM_NEG = decoder_1_out2 ? subtractor_2_bout : 1'bz;  // Controlled_Buffer controlled_buffer_6
  assign out_4 = decoder_1_out3 ? multiplier_1_out : 8'bz;  // Controlled_Buffer controlled_buffer_7
  assign out_4 = decoder_1_out4 ? divider_1_out : 8'bz;  // Controlled_Buffer controlled_buffer_8
  assign out_4 = decoder_1_out5 ? divider_2_out : 8'bz;  // Controlled_Buffer controlled_buffer_9
  assign out_4 = decoder_1_out6 ? negator_1_out : 8'bz;  // Controlled_Buffer controlled_buffer_10
  assign out_4 = decoder_1_out7 ? negator_2_out : 8'bz;  // Controlled_Buffer controlled_buffer_11
  assign out_4 = decoder_1_out8 ? not_1_out : 8'bz;  // Controlled_Buffer controlled_buffer_12
  assign out_4 = decoder_1_out9 ? not_2_out : 8'bz;  // Controlled_Buffer controlled_buffer_13
  assign out_4 = decoder_1_out10 ? and_1_out : 8'bz;  // Controlled_Buffer controlled_buffer_14
  assign out_4 = decoder_1_out11 ? or_2_out : 8'bz;  // Controlled_Buffer controlled_buffer_15
  assign out_4 = decoder_1_out12 ? xor_1_out : 8'bz;  // Controlled_Buffer controlled_buffer_16
  assign out_4 = decoder_1_out13 ? nand_1_out : 8'bz;  // Controlled_Buffer controlled_buffer_17
  assign out_4 = decoder_1_out14 ? nor_1_out : 8'bz;  // Controlled_Buffer controlled_buffer_18
  assign out_4 = decoder_1_out15 ? xnor_1_out : 8'bz;  // Controlled_Buffer controlled_buffer_19
  BitFinder bitfinder_1 (.in(divider_2_rem), .found(bitfinder_1_found));  // open: index
  and and_2 (and_2_out, decoder_1_out5, bitfinder_1_found);
  BitFinder bitfinder_2 (.in(divider_1_rem), .found(bitfinder_2_found));  // open: index
  and and_3 (and_3_out, decoder_1_out4, bitfinder_2_found);
  or or_3 (RESTO_DIV, and_2_out, and_3_out);
  nor nor_2 (NUM_0, out_4[7], out_4[6], out_4[5], out_4[4], out_4[3], out_4[2], out_4[1], out_4[0]);

  // Notes on the sheet:
  //   RIS
endmodule
